# Fritzing sketch bouton_led_alimentee_arduino (saved by Fritzing 0.9.4)
breadboards: 1

parts:
  Composant1 = Arduino Uno (Rev3)
  LED1 = LED - 5mm [color="Red (633nm)" package="5 mm [THT]"]
  S1 = Pushbutton [package="[THT]"]
  R1 = Resistor [tolerance=±5% resistance=220 package=THT]

nets:
  N1: Composant1.GND, LED1.cathode
  N2: Composant1.5V, S1.Pin_3, S1.Pin_4
  N3: LED1.anode, R1.Pin_1
  N4: S1.Pin_1, S1.Pin_2, R1.Pin_0
