# Fritzing sketch 2_leds_potentionmetre (saved by Fritzing 0.9.4)
breadboards: 1

parts:
  LED1 = LED - 5mm [color="Red (633nm)" package="5 mm [THT]"]
  LED2 = LED - 5mm [color="Red (633nm)" package="5 mm [THT]"]
  R1 = Resistor [tolerance=±5% resistance=220 package=THT]
  R2 = Resistor [tolerance=±5% resistance=220 package=THT]
  R3 = TRIMPOT [package=trimpot_pth_s3_lock]
  Composant1 = Arduino Uno (Rev3)

nets:
  N1: LED1.cathode, LED2.cathode, R3.CCW, Composant1.GND
  N2: LED1.anode, R1.Pin_0
  N3: LED2.anode, R2.Pin_0
  N4: R1.Pin_1, Composant1.D10_PWM/SS
  N5: R2.Pin_1, Composant1.D9_PWM
  N6: R3.WIPER, Composant1.A0
  N7: R3.CW, Composant1.5V
