# Fritzing sketch SketchPotentiometreAvec2DELS (saved by Fritzing 0.9.4)
circuit board: 6.88566cm x 5.36311cm
breadboards: 1

parts:
  LED2 = LED - 5mm [color="Green (555nm)" package="5 mm [THT]"]
  R1 = Resistor [tolerance=±5% resistance=220 package=THT]
  R2 = Resistor [tolerance=±5% resistance=220 package=THT]
  Bauteil1 = Arduino Uno (Rev3)
  R3 = Rotary Potentiometer (Large) [maximum_resistance=100kΩ package=THT]
  LED1 = LED - 5mm [color="Red (633nm)" package="5 mm [THT]"]

nets:
  N1: LED2.cathode, Bauteil1.GND, R3.leg1, LED1.cathode
  N2: LED2.anode, R2.Pin_1
  N3: R1.Pin_0, Bauteil1.D10_PWM/SS
  N4: R1.Pin_1, LED1.anode
  N5: R2.Pin_0, Bauteil1.D9_PWM
  N6: Bauteil1.A0, R3.wiper
  N7: Bauteil1.5V, R3.leg2

notes:
  FLIP FLOP

// code stored in the sketch: FlipFlop.ino
/*
  Flip Flop
  switching between two LEDs using a button
  
  This example is part of the Fritzing Creator Kit: www.fritzing.org/creator-kit.
*/

int buttonPin=2;                       // Pin where the button is attached
int greenLED=9;                        // Pin where the green LED is attached
int redLED=10;                         // Pin where the red LED is attached 

void setup(){
  pinMode(buttonPin, INPUT);           // button is initialised as INPUT 
  pinMode(greenLED, OUTPUT);           // green LED pin is initialised as OUTPUT 
  pinMode(redLED, OUTPUT);             // red LED pin is initialised as OUTPUT  
}

void loop(){
  if (digitalRead(buttonPin)==LOW){    // if the button is pressed (LOW) 
    digitalWrite(greenLED, HIGH);      // switch on green LED
    digitalWrite(redLED, LOW);         // switch off red LED
  } else {                             // else (if button is not pressed)
    digitalWrite(greenLED, LOW);       // switch off green LED
    digitalWrite(redLED, HIGH);        // switch on red LED
  }
}

// code stored in the sketch: Workshop_03_FlipFlop-w-Button.ino
int buttonPin=2;
int greenLED=9;
int redLED=10;

void setup(){
  pinMode(buttonPin, INPUT);
  pinMode(greenLED, OUTPUT);
  pinMode(redLED, OUTPUT);
}
void loop(){
  if (digitalRead(buttonPin)==LOW){
    digitalWrite(greenLED, HIGH);
    digitalWrite(redLED, LOW);
  } 
  else {
    digitalWrite(greenLED, LOW);
    digitalWrite(redLED, HIGH);
  }
}
