# Fritzing sketch del_commandee_par_bouton (saved by Fritzing 0.9.4)
breadboards: 1

parts:
  R2 = Resistor [tolerance=±5% resistance=220 package=THT]
  LED1 = LED - 5mm [color="Red (633nm)" package="5 mm [THT]"]
  S1 = Pushbutton [package="[THT]"]
  R3 = Resistor [tolerance=±5% resistance=220 package=THT]
  Bauteil3 = Arduino Uno (Rev3)

nets:
  N1: R2.Pin_0, Bauteil3.D10_PWM/SS
  N2: R2.Pin_1, LED1.anode
  N3: LED1.cathode, S1.Pin_1, S1.Pin_2, Bauteil3.GND
  N4: S1.Pin_3, S1.Pin_4, R3.Pin_1, Bauteil3.D2
  N5: R3.Pin_0, Bauteil3.5V
