# Fritzing sketch del_bouton_alimentee_par_arduino (saved by Fritzing 0.9.4)
breadboards: 1

parts:
  Bauteil2 = Arduino Uno (Rev3)
  R1 = Resistor [tolerance=±5% resistance=220 package=THT]
  S1 = Pushbutton [package="[SMD]"]
  LED1 = LED - 5mm [color="Red (633nm)" package="5 mm [THT]"]

nets:
  N1: Bauteil2.GND, S1.Pin_1, S1.Pin_2
  N2: Bauteil2.5V, R1.Pin_0
  N3: R1.Pin_1, LED1.anode
  N4: S1.Pin_3, S1.Pin_4, LED1.cathode
