# Fritzing sketch boutonEntree (saved by Fritzing 0.9.4)
breadboards: 1

parts:
  Composant1 = Arduino Uno (Rev3)
  S7 = Momentary Switch [package=ksa_sealed_tac_switch]
  R1 = Resistor [tolerance=±5% resistance=220 package="0603 [SMD]"]
  LED1 = smd LED [color="Red (633nm)" package="0805 [SMD]"]
  R2 = Resistor [tolerance=±5% resistance=1k package="0603 [SMD]"]

nets:
  N1: Composant1.D2, S7.3
  N2: Composant1.D3_PWM, LED1.anode
  N3: Composant1.5V, R2.Pin_1
  N4: Composant1.GND, S7.2, R1.Pin_0
  N5: S7.4, R2.Pin_0
  N6: R1.Pin_1, LED1.cathode
